# Fritzing sketch ESP32 Diagram (saved by Fritzing 1.0.5)

parts:
  esp1 = ESP32 DevKitc V4
  Part1 = PN532 Elechouse RFID NFC Module V3
  Part2 = ws2812b [package="smd 2812b"]

nets:
  N1: esp1.IO17, Part2.DIN
  N2: esp1.IO5, Part1.SS
  N3: esp1.GND#18, Part1.GND
  3V3: esp1.3V3, Part1.VCC
  N4: esp1.IO14, Part1.SCK
  N5: esp1.IO12, Part1.MISO
  N6: esp1.GND#32, Part2.VSS
  N7: esp1.IO13, Part1.MOSI
  5V: esp1.5V, Part2.VDD

custom parts:
  ESP32 DevKitc V4: ESP32-DevKitC board with ESP32-WROOM-32 module. ESP32-DevKitC V4 is a small-sized ESP32-based development board produced by Espressif. Most of the pins on the ESP module are broken out to the pin headers on the board. The pins D0, D1, D2, D3, CMD and CLK are used internally for communication between ESP32 and SPI flash memory. They are grouped on both sides near the USB connector. Avoid using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
  PN532 Elechouse RFID NFC Module V3: NFC is a popular technology in recent years. We often heard this work while smart phone company such as Samsung or HTC introduces their latest high-end phones. Almost all the high-end phone in the market support NFC. Near field communication (NFC) is a set of standards for smart phones and similar devices to establish radio communication with each other by touching them together or bringing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
